# Fritzing sketch ratpack_workshop (saved by Fritzing 0.7.4b)
breadboards: 1

parts:
  LED1 = LED - 5mm [color="Green (555nm)" package="5 mm [THT]"]
  S1 = Pushbutton [package=THT]
  R1 = Resistor [tolerance=±5% resistance=10k package=THT]
  Arduino1 = Arduino

nets:
  N1: LED1.cathode, R1.Pin_0, Arduino1.GND
  N2: LED1.anode, Arduino1.D9
  N3: S1.leg0, Arduino1.+5V
  N4: S1.leg1, R1.Pin_1, Arduino1.D2
